# Fritzing sketch Schematic (saved by Fritzing 0.9.3b)

parts:
  Mod1 = Raspberry Pi Pico
  S1 = Pushbutton [package=THT]
  S2 = Pushbutton [package=THT]
  S3 = Pushbutton [package=THT]
  S4 = Pushbutton [package=THT]
  S5 = Pushbutton [package=THT]
  S6 = Pushbutton [package=THT]
  S7 = Pushbutton [package=THT]
  S8 = Pushbutton [package=THT]
  S9 = Pushbutton [package=THT]
  S10 = Pushbutton [package=THT]
  LED1 = LED - 5mm [color="Blue (470nm)" package="5 mm [THT]"]  # not connected
  R1 = Resistor [tolerance=±5% resistance=220 package=THT]  # not connected
  LED2 = LED - 5mm [color="Blue (470nm)" package="5 mm [THT]"]  # not connected
  R2 = Resistor [tolerance=±5% resistance=220 package=THT]
  LED3 = LED - 5mm [color="Yellow (595nm)" package="5 mm [THT]"]  # not connected
  R3 = Resistor [tolerance=±5% resistance=220 package=THT]
  LED4 = LED - 5mm [color="Red (635nm)" package="5 mm [THT]"]
  R4 = Resistor [tolerance=±5% resistance=220 package=THT]
  LED5 = LED - 5mm [color="Red (635nm)" package="5 mm [THT]"]  # not connected
  R5 = Resistor [tolerance=±5% resistance=220 package=THT]
  LED6 = LED - 5mm [color="Blue (470nm)" package="5 mm [THT]"]  # not connected
  LED7 = LED - 5mm [color="Blue (470nm)" package="5 mm [THT]"]  # not connected
  LED8 = LED - 5mm [color="Red (635nm)" package="5 mm [THT]"]
  LED9 = LED - 5mm [color="Red (635nm)" package="5 mm [THT]"]  # not connected
  LED10 = LED - 5mm [color="Yellow (595nm)" package="5 mm [THT]"]  # not connected
  R6 = Resistor [tolerance=±5% resistance=220 package=THT]
  R7 = Resistor [tolerance=±5% resistance=220 package=THT]
  R8 = Resistor [tolerance=±5% resistance=220 package=THT]
  R9 = Resistor [tolerance=±5% resistance=220 package=THT]
  R10 = Resistor [tolerance=±5% resistance=220 package=THT]
  S11 = Pushbutton [package="[THT]"]
  S12 = Pushbutton [package="[THT]"]

nets:
  N1: Mod1.pin_1, S9.leg1
  N2: Mod1.pin_2, R9.Pin_1
  N3: Mod1.pin_3, Mod1.pin_18, Mod1.pin_33, Mod1.pin_38, S1.leg0, S2.leg0, S3.leg0, S4.leg0, S5.leg0, S6.leg0, S7.leg0, S8.leg0, S9.leg0, S10.leg0, LED4.cathode, LED8.cathode, S11.Pin_3, S11.Pin_4, S12.Pin_3, S12.Pin_4
  N4: Mod1.pin_4, S6.leg1
  N5: Mod1.pin_5, R6.Pin_1
  N6: Mod1.pin_6, S10.leg1
  N7: Mod1.pin_7, R8.Pin_1
  N8: Mod1.pin_9, S4.leg1
  N9: Mod1.pin_10, R5.Pin_1
  N10: Mod1.pin_11, S5.leg1
  N11: Mod1.pin_12, R2.Pin_1
  N12: Mod1.pin_14, S2.leg1
  N13: Mod1.pin_15, R3.Pin_1
  N14: Mod1.pin_19, S11.Pin_1, S11.Pin_2
  N15: Mod1.pin_20, S12.Pin_1, S12.Pin_2
  N16: Mod1.pin_21, R7.Pin_1
  N17: Mod1.pin_22, S7.leg1
  N18: Mod1.pin_25, S3.leg1
  N19: Mod1.pin_26, R4.Pin_1
  N20: Mod1.pin_27, S1.leg1
  N21: Mod1.pin_31, R10.Pin_1
  N22: Mod1.pin_32, S8.leg1

notes:
  Service
  Test
  To Addressable LEDs
  (optional)

custom parts:
  Raspberry Pi Pico: Raspberry Pi Pico. Based around the RP2040 microcontroller the Pico is a low cost microcontroller device bringing Raspberry Pi quality, cost, and easy of use to the microcontroller space. Jan 2021, Split part in to two versions: tht (this one) and SMD. This one will drill holes for a .1 in header in pcb to allow plugging in the module as well as providing pads to solder the module to the top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
